# Fritzing sketch rover_circuit (saved by Fritzing 0.9.3b)

parts:
  U1 = LuaNode32 / ESP32 [part_number=ESP32S-PIN30]
  M1 = DC Mini Metal Gear Motor
  M2 = DC Mini Metal Gear Motor
  BAT1 = BC9VPC [package=bc9vpc]
  U2 = Texas Instruments DRV8833

nets:
  N1: U1.D25, U2.IN4
  N2: U1.D26, U2.IN3
  N3: U1.D27, U2.EEP
  N4: U1.RX2, U2.IN2
  N5: U1.TX2, U2.IN1
  N6: M1.IN1, U2.OUT1
  N7: M1.IN2, U2.OUT2
  N8: M2.IN1, U2.OUT3
  N9: M2.IN2, U2.OUT4
  N10: BAT1.V+, U2.VCC
  N11: BAT1.V-, U2.GND

custom parts:
  LuaNode32 / ESP32: New Image for LuaNode32 DOIT ESP32 DEVKIT V1. Base parts from LuaNode32 / ESP32 ESP32 based LuaNode32 by G.Noorlander DOIT Esp32 DevKit v1 (30 pins long, 11 pins width) by Werner Rothschopf (modified by vanepp Dec 2018)
  Texas Instruments DRV8833: The DRV8833 provides a dual bridge motor driver solution for toys, printers, and other mechatronic applications.
